# Fritzing sketch MasterFritzingWithoutMPU (saved by Fritzing 1.0.6)
breadboards: 1

parts:
  Part1 = Adafruit QT Py ESP32 Pico [mn=Adafruit mpn="Adafruit #5395" part_number="Adafruit #5395"]
  Part3 = Adafruit PAM8302 [part_number="Adafruit #2130"]
  U1 = WS2812 RGB LED strip
  SP1 = SPEAKER [package=pcb_mount_speaker]

nets:
  GND: Part1.GND, Part3.GND, Part3.AIN-, U1.GND
  N1: Part1.A0, Part3.AIN+
  N2: Part1.A2, U1.DIN
  3.3V: Part1.3.3V, Part3.VCC
  +5V: Part1.+5V, U1.VCC
  N3: Part3.VO+, SP1.-
  N4: Part3.VO-, SP1.+

custom parts:
  Adafruit PAM8302: This super small mono amplifier is surprisingly powerful - able to deliver up to 2.5 Watts into 4-8 ohm impedance speakers. Inside the miniature chip is a class D controller, able to run from 2.0V-5.5VDC. Since the amp is a class D, its very efficient (over 90% efficient when driving an 8Ω speaker at over half a Watt) - making it perfect for portable and battery-powered projects. It has built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
  WS2812 RGB LED strip: WS2812 strip
